# Fritzing sketch Truckasaurus (saved by Fritzing 1.0.2b)

parts:
  Teensy1 = Teensy 4.1
  Part1 = InvenSense MPU6050
  Camera_Tilt_Servo = Dagu DGServo 9g (End View) [part_number=RS001B]
  Camera_Pan_Servo = Dagu DGServo 9g (End View) [part_number=RS001B]
  CH1_(a) = Dagu DGServo 9g header connector (female) [package=THT]
  CH1_(b) = Dagu DGServo 9g header connector (female) [package=THT]
  CH2 = Dagu DGServo 9g header connector (female) [package=THT]
  CH3 = Dagu DGServo 9g header connector (female) [package=THT]
  Steering_Servo = Dagu DGServo 9g (End View) [part_number=RS001B]
  Motor_ESC = Dagu DGServo 9g header connector (female) [package=THT]

nets:
  GND: Teensy1.GND, Teensy1.GND2#55, CH1_(b).gnd, CH2.gnd, Motor_ESC.gnd
  N1: Teensy1.D3, CH2.pulse
  N2: Teensy1.D4, CH1_(a).pulse
  N3: Teensy1.D5, Motor_ESC.pulse
  N4: Teensy1.D6, Steering_Servo.pulse
  N5: Teensy1.D10, Camera_Tilt_Servo.pulse
  N6: Teensy1.D11, Camera_Pan_Servo.pulse
  N7: Teensy1.A4/D18, Part1.SDA
  N8: Teensy1.A5/D19, Part1.SCL
  N9: Teensy1.3V3_LOW, Part1.VCC
  N10: Teensy1.GND2#31, Part1.GND
  GND_2: Camera_Tilt_Servo.gnd, Camera_Pan_Servo.gnd, CH3.gnd
  VCC: Camera_Tilt_Servo.vcc, CH3.Vcc
  VCC_2: Camera_Pan_Servo.vcc, CH1_(b).Vcc
  GND_3: CH1_(a).gnd, Steering_Servo.gnd
  VCC_3: CH1_(a).Vcc, Steering_Servo.vcc
  VCC_4: CH2.Vcc, Motor_ESC.Vcc

notes:
  XL5 ESC
  Receiver
  TQ 3Ch
  Pan
  Truckasaurus
  Tilt
  Steer
  ESC and 5V Batt. Grounds are connected

custom parts:
  Teensy 4.1: The Teensy is a complete USB-based microcontoller development system, in a very small footprint, capable of implementing many types of projects. All programming is done via the USB port. No special programmer is needed, only a standard micro-USB cable and a PC or Macintosh with a USB port.
